# Fritzing sketch wiring-diagram (saved by Fritzing 0.9.3b)

parts:
  LCD3 = TFT 1.8 inch 160x128 w SD
  R2 = Resistor [tolerance=±5% resistance=220 package=THT]
  IR1 = TSOP312.., 314.. [package=THT]
  LED2 = LEDs [package=led10mm]
  C1 = Capacitor [package=cap-pth-small2]
  Q2 = NPN-Transistor [package="SOT-23 [SMD]"]
  R3 = Resistor [tolerance=±5% resistance=1k package=THT]
  R4 = Resistor [tolerance=±5% resistance=100 package=THT]
  R5 = Resistor [tolerance=±5% resistance=100k package=THT]
  R6 = Resistor [tolerance=±5% resistance=100k package=THT]
  C2 = Capacitor [package=cap-pth-small2]
  S1 = Toggle Switch [package=THT]
  Componente5 = Black Joystick KY-023
  M4 = ESP32-S2-DevKitC-1 [part_number=ESP32-S2-DevKitC-1]
  JP25 = Header 1 [package=1x01_offset]
  JP26 = Header 1 [package=1x01_offset]
  JP27 = Header 1 [package=1x01_offset]
  JP28 = Header 1 [package=1x01_offset]
  JP29 = Header 1 [package=1x01_offset]
  JP30 = Header 1 [package=1x01_offset]
  JP31 = Header 1 [package=1x01_offset]
  JP32 = Header 1 [package=1x01_offset]
  M5 = NRF24L01-BO [package=THT]
  Componente6 = PN532 Elechouse RFID NFC Module V3
  A2 = u-blox NEO-6M GPS Breakout
  BAT1 = 18650 battery holder [package=battery-18650-kit]
  A3 = j5019

nets:
  +5V: LCD3.pin_1, IR1.Data, C1.2, R4.Pin_0, Componente5.+5V, M4.pin_1, M4.pin_2, JP26.1, Componente6.VCC
  GND: LCD3.pin2, IR1.Vs, C1.1, Q2.2, R6.Pin_0, Componente5.GND, M4.pin_22, M4.pin_44, JP25.1, Componente6.GND, A2.Pin_2, BAT1.-, A3.Pin_2, A3.Pin_5
  N1: LCD3.pin3, M4.pin_9
  N2: LCD3.pin4, M4.pin_8
  N3: LCD3.pin_5, M4.pin_7
  N4: LCD3.pin_6, LCD3.pin_10, M4.pin_6, M5.M0
  N5: LCD3.pin_7, LCD3.pin_12, M4.pin_5, M5.SCK
  N6: LCD3.pin_8, R2.Pin_0
  N7: LCD3.pin_9, M4.pin_37
  N8: LCD3.pin_11, M4.pin_38, M5.M1
  N9: R2.Pin_1, M4.pin_4
  N10: IR1.GND, M4.pin_40
  N11: LED2.C, Q2.1
  N12: LED2.A, R4.Pin_1
  N13: Q2.0, R3.Pin_1
  N14: R3.Pin_0, M4.pin_41
  N15: R5.Pin_0, C2.2, M5.GND, BAT1.+, A3.Pin_6
  N16: R5.Pin_1, R6.Pin_1, C2.1
  N17: S1.L1, A3.Pin_1
  N18: S1.COM, M4.pin_21, JP27.1, M5.VCC, A2.Pin_1
  N19: Componente5.SW, M4.pin_20
  N20: Componente5.VRy, M4.pin_19
  N21: Componente5.VRx, M4.pin_18
  N22: M4.pin_10, JP29.1, A2.Pin_4
  N23: M4.pin_11, JP30.1, Componente6.SDA
  N24: M4.pin_12, JP32.1, Componente6.SCL
  N25: M4.pin_15, JP28.1
  N26: M4.pin_27, M5.CE
  N27: M4.pin_28, M5.CSN
  N28: M4.pin_32, M5.IRQ
  N29: M4.pin_35, JP31.1, A2.Pin_3

notes:
  100k ohms
  100nF
  104
  1k ohms
  100 ohms
  IR RX
  IR TX
  2N2222
  220 ohms
  18650
  Battery charger and
  voltage regulator
  5V out
  Battery in
  3.3V out
  5V in
  NRF24L01
  330 ohms
  Lithium battery
  ST7735 DRIVER
  @viniciushnf
  GPIO 21
  GPIO 47
  1838
  NRF24L01 with adapter
  --- DISPLAY ---
  LED BL -> 4
  SCK (SCLK) -> 5
  SDA (MOSI) -> 6
  AO (DC) -> 7
  RESET -> 15
  CS -> 16
  --- SD CARD ---
  CS -> 40
  MOSI -> 6
  MISO -> 41
  SCK -> 5
  -- NRF24L01 --
  CE -> 21
  CSN/SS -> 47
  SCK -> 5
  MOSI -> 6
  MISO -> 41
  IRQ -> 35
  -- JOYSTICK --
  VR-X -> 12
  VR-Y -> 13
  SW -> 14
  ---- I2C ----
  SDA -> 18
  SCL -> 8
  ----- IR -----
  TX -> 1
  RX -> 2
  --- GPS ---
  TX -> 38
  RX -> 17
  ---- BAT ----
  BAT -> 10
  GND
  5 V
  3.3 V
  LED BL
  IR
  MEANING OF THE COLOR OF THE THREAD
  JOYSTICK AXIS
  SHARED SPI
  JOYSTICK BUTTON
  VBAT ADC
  DEDICATED SPI
  Developed by Vinicius Henrique
  - https://github.com/viniciushnf
  Bruce Firmware:
  - https://bruce.computer/
  --- SHARED SPI ---
  SCK -> 5
  MOSI -> 6
  MISO -> 41
  I recommend testing everything on a breadboard first. Check the pinout and specifications of your modules.
  --------- Extra Pins ----------
  Power: GND, 3.3V, 5V
  GPIO: 9, 8, 18, 17 and 38
  Switch on/off
  Extra Pins
  BAT +
  The adapter for the NRF24L01 is important because the module is very sensitive to power supply.
  Joystick
  PN532
  NEO-6M
  Li-ion Battery
  https://github.com/viniciushnf/ESP32-S3-Bruce-ST7735-1.8
  pin header
  connector
  J5019

custom parts:
  TFT 1.8 inch 160x128 w SD: This is a generic 1.8 tft spi lcd display available on ebay and others. The 1.8" display has 128x160 color pixels.
  Black Joystick KY-023: Description: The joystick is a combination of 2 analoog potentiometer and a digital switch. Arduino GND --> Module pin - Arduino +5V --> Module pin +5V Arduino Analoog 0 --> Module VRx Arduino Analoog 1 --> Module VRy Arduino Digital --> Module SW Dimensions: 1" x 1.25"
  ESP32-S2-DevKitC-1: ESP32-S2-DevKitC-1 is an entry-level development board based on ESP32-S2-SOLO (on-board PCB antenna). It is based on the ESP32 microcontroller that boasts Wifi, Bluetooth, Ethernet and Low Power support all in a single chip. (vanepp) Feb 2022: converted to ESP32-S2-DevKitC-1. This module is 44pins long (2x22) and 11 pins width.
  NRF24L01-BO: NRF24L01-BO breakout board for the NRF24L01. Pcb view suppressed as unneeded.
  PN532 Elechouse RFID NFC Module V3: NFC is a popular technology in recent years. We often heard this work while smart phone company such as Samsung or HTC introduces their latest high-end phones. Almost all the high-end phone in the market support NFC. Near field communication (NFC) is a set of standards for smart phones and similar devices to establish radio communication with each other by touching them together or bringing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
  18650 battery holder: 18650 Battery Holder identical to the dual battery version.
  j5019: This module is a small single cell lithium battery charging module which also includes a 1A step-up (boost) converter for powering a large range of applications.
